# Fritzing sketch TpSynth (saved by Fritzing 0.9.8b)
breadboards: 1

parts:
  Mod1 = Raspberry Pi 4B
  HC-SR04_Sensor_1 = HC-SR04 Ultrasonic Distance Sensor
  DHT1 = DHT11 Humitidy and Temperature Sensor
  R1 = Resistor [tolerance=±5% resistance=1k package="0603 [SMD]"]
  R2 = Resistor [tolerance=±5% resistance=1k package="0603 [SMD]"]
  R3 = Resistor [tolerance=±5% resistance=1k package="0603 [SMD]"]
  R4 = Resistor [tolerance=±5% resistance=10k package="0603 [SMD]"]

nets:
  3V3: Mod1.3V3, DHT1.VDD, R4.Pin_0
  5V: Mod1.5V, HC-SR04_Sensor_1.VCC
  GND: Mod1.GND, HC-SR04_Sensor_1.GND, DHT1.GND, R1.Pin_1
  N1: Mod1.GPIO4, DHT1.DATA, R4.Pin_1
  N2: Mod1.GPIO19, R2.Pin_0, R3.Pin_1
  N3: Mod1.GPIO26, HC-SR04_Sensor_1.TRIG
  N4: HC-SR04_Sensor_1.ECHO, R3.Pin_0
  N5: R1.Pin_0, R2.Pin_1

custom parts:
  DHT11 Humitidy and Temperature Sensor: DHT11 Humidity and Temperature Sensor
